# Fritzing sketch Sound_Sensor (saved by Fritzing 0.9.3b)
breadboards: 1

parts:
  Part1 = Arduino Uno (Rev3) - ICSP
  J1 = Piezo Speaker
  LED1 = smd LED [color="Blue (505nm)" package="0603 [SMD]"]
  LED2 = smd LED [color="Blue (505nm)" package="0603 [SMD]"]
  R1 = Resistor [tolerance=±5% resistance=1k package="2512 [SMD]"]
  R2 = Resistor [tolerance=±5% resistance=1k package="0402 [SMD]"]
  hc-sr1 = hc-sr04

nets:
  N1: Part1.ICSP_MISO, Part1.D12/MISO, hc-sr1.Echo
  GND: Part1.GND, J1.pin1, R1.Pin_0, R2.Pin_0, hc-sr1.GND
  N2: Part1.D13/SCK, hc-sr1.Trig
  N3: Part1.D3_PWM, J1.pin2
  N4: Part1.D6_PWM, LED1.anode
  N5: Part1.D7, LED2.anode
  5V: Part1.5V, hc-sr1.VCC
  N6: LED1.cathode, R1.Pin_1
  N7: LED2.cathode, R2.Pin_1
